// Logisim project 000_Decoder.circ as structural Verilog: 2 circuits, main circuit main
module main (
  input  x2,
  input  x1,
  input  e,
  input  x2_2,
  input  x1_2,
  input  [1:0] in_6,
  input  Enable,
  input  [1:0] Input,
  output y1,
  output y1_2,
  output y2,
  output y2_2,
  output y3,
  output y3_2,
  output y4,
  output y4_2,
  output [3:0] out_17,
  output [3:0] Output
);

  wire not_1_out, not_2_out, not_3_out, not_4_out, not_5_out, not_6_out;

  not not_1 (not_1_out, x2);
  not not_2 (not_2_out, x1);
  and and_1 (out_17[0], not_4_out, not_3_out);
  and and_2 (out_17[1], not_4_out, in_6[0]);
  and and_3 (out_17[2], in_6[1], not_3_out);
  and and_4 (out_17[3], in_6[1], in_6[0]);
  not not_3 (not_3_out, in_6[0]);
  not not_4 (not_4_out, in_6[1]);
  and and_5 (y1, not_1_out, not_2_out);
  and and_6 (y2, not_1_out, x1);
  and and_7 (y3, x2, not_2_out);
  and and_8 (y4, x2, x1);
  Decoder #(.select(2)) decoder_1 (
    .out0(Output[0]), .out1(Output[1]), .out2(Output[2]), .out3(Output[3]), .sel(Input), .en(Enable));
  not not_5 (not_5_out, x2_2);
  and and_9 (y1_2, not_5_out, e, not_6_out);
  and and_10 (y2_2, not_5_out, e, x1_2);
  and and_11 (y3_2, x2_2, e, not_6_out);
  and and_12 (y4_2, x2_2, e, x1_2);
  not not_6 (not_6_out, x1_2);

  // Notes on the sheet:
  //   2-bit Decoder
  //   Using a Bus
  //   Individual Inputs
  //   y1=(x1)' * (x2)'
  //   y2=x1 * (x2)'
  //   y3=(x1)' * x2
  //   y4=x1 * x2
  //   Decoder: (Binary-Enoding) -> (One-Hot-Encoding)
  //   with Enable
  //   y1=(x1)' * (x2)'
  //   y2=x1 * (x2)'
  //   y3=(x1)' * x2
  //   y4=x1 * x2
endmodule

module _2_bit_Decoder (
  input  x1,
  input  x2,
  output y1,
  output y2,
  output y3,
  output y4
);

  wire not_1_out, not_2_out, not_3_out, not_4_out;

  not not_1 (not_1_out, x1);
  not not_2 (not_2_out, x2);
  not not_3 (not_3_out, x1);
  not not_4 (not_4_out, x2);
  and and_1 (y4, x1, x2);
  and and_2 (y1, not_1_out, not_2_out);
  and and_3 (y2, not_3_out, x2);
  and and_4 (y3, x1, not_4_out);
endmodule
