// Logisim project 000_Decoder_and_MUX.circ as structural Verilog: 1 circuit, main circuit main
module main (
  input  in_1,
  input  in_2,
  input  in_3,
  input  in_4,
  input  in_5,
  input  in_6,
  input  in_7,
  input  in_8,
  input  [1:0] in_9,
  input  in_10,
  input  in_11,
  input  in_12,
  output out_13,
  output out_14,
  output out_15,
  output out_16,
  output out_17,
  output [3:0] out_18,
  output out_19,
  output out_20,
  output out_21
);

  wire and_9_out, and_10_out, and_11_out, and_12_out, clock_1_out, not_1_out, not_2_out, not_3_out,
       not_4_out, not_5_out, not_6_out;

  Clock clock_1 (.out(clock_1_out));
  D_Flip_Flop d_ff_1 (.clk(in_10), .D(in_11), .Q(out_19));  // open: Qn, preset, en, reset
  D_Flip_Flop d_ff_2 (.clk(clock_1_out), .D(in_12), .Q(out_20));  // open: Qn, preset, en, reset
  not not_1 (not_1_out, in_5);
  not not_2 (not_2_out, in_6);
  and and_1 (out_18[0], not_3_out, not_4_out);
  and and_2 (out_18[1], not_3_out, in_9[0]);
  and and_3 (out_18[2], in_9[1], not_4_out);
  and and_4 (out_18[3], in_9[1], in_9[0]);
  not not_3 (not_3_out, in_9[1]);
  not not_4 (not_4_out, in_9[0]);
  D_Flip_Flop d_ff_3 (.clk(clock_1_out), .D(in_12), .Q(out_21));  // open: Qn, preset, en, reset
  and and_5 (out_13, not_1_out, not_2_out);
  and and_6 (out_14, not_1_out, in_6);
  and and_7 (out_15, in_5, not_2_out);
  and and_8 (out_17, in_5, in_6);
  and and_9 (and_9_out, in_1, not_6_out, not_5_out);
  and and_10 (and_10_out, in_2, not_6_out, in_8);
  and and_11 (and_11_out, in_3, in_7, not_5_out);
  and and_12 (and_12_out, in_4, in_7, in_8);
  not not_5 (not_5_out, in_8);
  not not_6 (not_6_out, in_7);
  or or_1 (out_16, and_9_out, and_10_out, and_11_out, and_12_out);

  // Notes on the sheet:
  //   2-bit Decoder
  //   Individual Inputs
  //   Using a Bus and Spitter
  //   4x1 MUX
endmodule
