// Logisim project 200_Register_Parallel-Load.circ as structural Verilog: 4 circuits, main circuit main
module main (
  input  in_1,
  input  in_2,
  input  in_3,
  input  in_4,
  input  in_5,
  input  in_6,
  input  in_7,
  input  in_8,
  input  in_9,
  input  in_10,
  input  in_11,
  input  in_12,
  input  [1:0] in_13,
  input  in_14,
  output out_15,
  output out_16,
  output out_17,
  output out_18,
  output out_19,
  output out_20,
  output [1:0] out_21
);

  wire clock_1_out, clock_2_out, clock_3_out, multiplexer_1_out, multiplexer_2_out, n2x1_mux_1_d,
       n2x1_mux_2_d, not_1_out, not_2_out;

  not not_1 (not_1_out, in_9);
  Clock clock_1 (.out(clock_1_out));
  _2x1_MUX u_2x1_mux_1 (.i0(out_16), .i1(in_1), .d(n2x1_mux_1_d), .s(in_5));
  Clock clock_2 (.out(clock_2_out));
  Multiplexer multiplexer_1 (.in0(in_7), .in1(out_19), .out(multiplexer_1_out), .sel(not_1_out), .en(1'b1));
  Clock clock_3 (.out(clock_3_out));
  _2x1_MUX u_2x1_mux_2 (.i0(out_17), .i1(in_2), .d(n2x1_mux_2_d), .s(in_5));
  D_Flip_Flop d_ff_1 (.clk(clock_2_out), .D(n2x1_mux_1_d), .Q(out_16));  // open: Qn, preset, en, reset
  Multiplexer multiplexer_2 (.in0(in_8), .in1(out_20), .out(multiplexer_2_out), .sel(not_1_out), .en(1'b1));
  D_Flip_Flop d_ff_2 (.clk(clock_1_out), .D(multiplexer_1_out), .Q(out_19));  // open: Qn, preset, en, reset
  _2_bit_Parallel_Load_Reg u_2_bit_parallel_load_reg_1 (
    .load(in_14), .clk(clock_3_out), .i1(in_13[1]), .i0(in_13[0]), .q1(out_21[1]), .q0(out_21[0]));
  D_Flip_Flop d_ff_3 (.clk(clock_2_out), .D(n2x1_mux_2_d), .Q(out_17));  // open: Qn, preset, en, reset
  D_Flip_Flop d_ff_4 (.clk(clock_1_out), .D(multiplexer_2_out), .Q(out_20));  // open: Qn, preset, en, reset
  not not_2 (not_2_out, in_12);
  Multiplexer multiplexer_3 (.in0(in_10), .in1(in_11), .out(out_18), .sel(not_2_out), .en(1'b1));
  _2x1_MUX u_2x1_mux_3 (.i0(in_4), .i1(in_3), .d(out_15), .s(in_6));

  // Notes on the sheet:
  //   2-bit Parallel-Load Register
  //   Using Custom 2x1 MUX
  //   4-bit Parallel-Load Register
endmodule

module _2x1_MUX (
  input  i0,
  input  i1,
  input  s,
  output d
);

  wire and_1_out, and_2_out, not_1_out;

  not not_1 (not_1_out, s);
  and and_1 (and_1_out, i0, not_1_out);
  and and_2 (and_2_out, i1, s);
  or or_1 (d, and_1_out, and_2_out);

  // Notes on the sheet:
  //   d=[i0 * (s0)'] + [i1 * s0]
endmodule

module _4x1_MUX (
  input  i0,
  input  i1,
  input  i2,
  input  i3,
  input  s1,
  input  s0,
  output d
);

  wire and_1_out, and_2_out, and_3_out, and_4_out, not_1_out, not_2_out;

  not not_1 (not_1_out, s1);
  and and_1 (and_1_out, i0, not_1_out, not_2_out);
  and and_2 (and_2_out, i1, not_1_out, s0);
  and and_3 (and_3_out, i2, s1, not_2_out);
  and and_4 (and_4_out, i3, s1, s0);
  not not_2 (not_2_out, s0);
  or or_1 (d, and_1_out, and_2_out, and_3_out, and_4_out);
endmodule

module _2_bit_Parallel_Load_Reg (
  input  i1,
  input  i0,
  input  load,
  input  clk,
  output q1,
  output q0
);

  wire n2x1_mux_1_p2, n2x1_mux_2_p3;

  // _2x1_MUX 2x1_mux_1: pin names not known; wires that end beside it: i1, n2x1_mux_1_p2, load
  // _2x1_MUX 2x1_mux_2: pin names not known; wires that end beside it: load, i0, n2x1_mux_2_p3, q0
  D_Flip_Flop d_ff_1 (.clk(clk), .D(n2x1_mux_1_p2), .Q(load));  // open: Qn, preset, en, reset
  D_Flip_Flop d_ff_2 (.clk(clk), .D(n2x1_mux_2_p3), .Q(q0));  // open: Qn, preset, en, reset

  assign q1 = load;

  // Notes on the sheet:
  //   2-bit Parallel-Load Register
endmodule
