// Logisim project CPU.circ as structural Verilog: 7 circuits, main circuit main
module main (
  input  in_1,
  output Signed_OverFlow,
  output equal
);

  wire MemWr, RegDst, RegWr;
  wire [4:0] instruction_memory_1_instr_15_11, instruction_memory_1_instr_20_16,
       instruction_memory_1_instr_25_21, mux_reg_file_1_zero_or_one;
  wire [5:0] instruction_memory_1_instr_5_0;
  wire [15:0] instruction_memory_1_instr_15_0;
  wire [23:0] memory_data_1_address_2, memory_data_temp_1_address;
  wire [31:0] adder_1_out_3, alu_1_result, four_1_four, memory_data_temp_1_instruction, program_counter_1_pc,
       register_file_1_read_data_1, register_file_1_read_data_2, sign_extend_1_out_2;

  four four_1 (.four(four_1_four));
  program_counter program_counter_1 (.PC(program_counter_1_pc));
  // Probe on program_counter_1_pc
  Adder adder_1 (.in_1(program_counter_1_pc), .in_2(four_1_four), .out_3(adder_1_out_3));
  Instruction_Memory instruction_memory_1 (
    .Read_Address(program_counter_1_pc), .Instr_25_21(instruction_memory_1_instr_25_21),
    .Instr_20_16(instruction_memory_1_instr_20_16), .Instr_15_11(instruction_memory_1_instr_15_11),
    .Instr_15_0(instruction_memory_1_instr_15_0), .Instr_5_0(instruction_memory_1_instr_5_0));
  // Probe on instruction_memory_1_instr_25_21
  // Probe on instruction_memory_1_instr_20_16
  // Probe on instruction_memory_1_instr_15_0
  MUX_Reg_File mux_reg_file_1 (
    .Zero(instruction_memory_1_instr_20_16), .One(instruction_memory_1_instr_15_11),
    .Zero_or_One(mux_reg_file_1_zero_or_one), .Control(RegDst));
  Sign_Extend sign_extend_1 (.in_1(instruction_memory_1_instr_15_0), .out_2(sign_extend_1_out_2));
  Register_File register_file_1 (
    .Read_Register_1(instruction_memory_1_instr_25_21), .Read_Register_2(instruction_memory_1_instr_20_16),
    .Write_Register(mux_reg_file_1_zero_or_one), .Read_Data_1(register_file_1_read_data_1),
    .Read_Data_2(register_file_1_read_data_2), .RegWrite(RegWr), .clk(in_1));  // open: Write_Data
  // Probe on register_file_1_read_data_1
  // Probe on sign_extend_1_out_2
  alu alu_1 (
    .Switch(4'b0101), .X(register_file_1_read_data_1), .Equal(equal), .Result(alu_1_result),
    .Signed_Overflow_18670403(Signed_OverFlow), .Y(sign_extend_1_out_2));
  // Probe on alu_1_result
  // Probe on memory_data_1_address_2
  // Probe on memory_data_temp_1_address
  memory_data memory_data_1 (
    .Address(alu_1_result), .Write_Data(register_file_1_read_data_2), .in_2(in_1), .in_3(MemWr),
    .address_2(memory_data_1_address_2));  // open: Read_Data
  memory_data_temp memory_data_temp_1 (
    .instruction(memory_data_temp_1_instruction), .fetch_addr(alu_1_result),
    .address(memory_data_temp_1_address));
  // Probe on memory_data_temp_1_instruction

  // Other names for the same wires on the sheet: clk = in_1

  // Notes on the sheet:
  //   rs
  //   rt
  //   -> ALU-Control
  //   ALU-Control (5=Add)
  //   Address
  //   Write-Data
endmodule

module Decode (
  input  [31:0] Instruction,
  output [5:0] opcode,
  output [4:0] RR1,
  output [4:0] RR2,
  output [15:0] out_5,
  output [5:0] func,
  output [4:0] out_7
);


  assign func = Instruction[5:0];
  assign opcode = Instruction[31:26];
  assign out_5 = Instruction[15:0];
  assign out_7 = Instruction[15:11];
  assign RR1 = Instruction[25:21];
  assign RR2 = Instruction[20:16];

  // Notes on the sheet:
  //   [26:31]
  //   [21:25]
  //   [16:20]
  //   [0:15]
  //   [0:5]
  //   [11:15]
endmodule

module Sign_Extend (
  input  [15:0] in_1,
  output [31:0] out_2
);

  assign out_2 = {{16{in_1[15]}}, in_1};  // Bit_Extender bit_extender_1
endmodule

module Instruction_Memory (
  input  [31:0] Read_Address,
  output [4:0] Instr_25_21,
  output [4:0] Instr_20_16,
  output [4:0] Instr_15_11,
  output [15:0] Instr_15_0,
  output [5:0] Instr_5_0
);

  wire [31:0] instruction_memory_1_instruction;

  instruction_memory instruction_memory_1 (.instruction(instruction_memory_1_instruction), .fetch_addr(Read_Address));
  Decode decode_1 (
    .Instruction(instruction_memory_1_instruction), .RR1(Instr_25_21), .RR2(Instr_20_16), .out_5(Instr_15_0),
    .func(Instr_5_0), .out_7(Instr_15_11));  // open: opcode
endmodule

module Register_File (
  input  [4:0] Read_Register_1,
  input  [4:0] Read_Register_2,
  input  [4:0] Write_Register,
  input  clk,
  input  RegWrite,
  input  [31:0] Write_Data,
  output [31:0] Read_Data_1,
  output [31:0] Read_Data_2
);

  regfile regfile_1 (
    .read_reg1(Read_Register_1), .read_reg2(Read_Register_2), .write_register(Write_Register),
    .Data(Write_Data), .write_enable(RegWrite), .clock(clk), .read_data1(Read_Data_1),
    .read_data2(Read_Data_2));  // open: reg_16_val, reg_17_val, reg_18_val, reg_19_val, reg_20_val
endmodule

module MUX_Reg_File (
  input  [4:0] Zero,
  input  [4:0] One,
  input  Control,
  output [4:0] Zero_or_One
);

  Multiplexer #(.width(5), .enable("false")) multiplexer_1 (.in0(Zero), .in1(One), .out(Zero_or_One), .sel(Control));
endmodule

module four (
  output [31:0] four
);


  assign four = 32'h4;
endmodule
